# Fritzing sketch Exo 2 SmartPatate (saved by Fritzing 0.9.3b)
breadboards: 1

parts:
  Composant1 = Arduino Uno (Rev3)
  C1 = Ceramic Capacitor [capacitance="100 nF" package="0805 [SMD, multilayer]"]
  LED1 = smd LED [color="Red (633nm)" package="0805 [SMD]"]
  R2 = Resistor [tolerance=±5% resistance=3.3k package="2512 [SMD]"]
  R3 = Resistor [tolerance=±5% resistance=10k package="2512 [SMD]"]
  L1 = Inductor [package="1206 [SMD]"]
  C2 = Tantalum Capacitor [capacitance="1 μF" package="B 3528 [SMD, tantalum]"]
  U3 = TOUCH [package=touch1]
  R1 = Resistor [tolerance=±5% resistance=1M package="1206 [SMD]"]

nets:
  N1: Composant1.A0, C1.1, LED1.cathode, R1.Pin_1
  N2: Composant1.D9_PWM, R3.Pin_1
  N3: Composant1.GND, C1.0, R2.Pin_0, R1.Pin_0
  N4: LED1.anode, L1.pin_1, C2.-
  N5: R2.Pin_1, R3.Pin_0, L1.pin_0
  N6: C2.+, U3.T1, U3.T2
